# Fritzing sketch DIY-lampe-multicouleur-controllabe-wi-fi (saved by Fritzing 0.9.3b)

parts:
  U1 = ESP8266 WiFi Module [part_number=ESP8266]
  NEOPIXEL1 = Neopixel Strip -- White (30/m)
  NEOPIXEL2 = Neopixel Strip -- White (30/m)
  NEOPIXEL3 = Neopixel Strip -- White (30/m)
  U2 = V_REG_LD1117VXX [package=78xxl]
  Power_plug1 = Power plug

nets:
  N1: U1.VCC, U2.OUT
  N2: U1.GPIO_2, NEOPIXEL1.Din
  GND: U1.GND, NEOPIXEL1.GND, NEOPIXEL3.GND#6
  N3: NEOPIXEL1.+5V, NEOPIXEL3.+5V#4
  N4: NEOPIXEL1.Dout, NEOPIXEL3.Din
  GND_2: NEOPIXEL2.GND#1, U2.GND, Power_plug1.GND
  N5: NEOPIXEL2.Din, NEOPIXEL3.Dout
  N6: NEOPIXEL2.+5V#3, U2.IN, Power_plug1.VCC
  N7: NEOPIXEL2.+5V#4, NEOPIXEL3.+5V#3
  N8: NEOPIXEL2.GND#6, NEOPIXEL3.GND#1

notes:
  alimentation 5v
  regulateur de tension 3.3v
  esp01
  3 rangés led rgb (ws2812)

custom parts:
  ESP8266 WiFi Module: Generic WiFi Module based on the ESP8266 with onboard PCB antenna and UART communications
  Neopixel Strip -- White (30/m): These NeoPixel strips have 30 digitally-addressable pixel LEDs per meter and are very affordable and are only 12.5 mm wide, 10 mm if you remove the strip from the casing.
