# Fritzing sketch conecteur ftdi (saved by Fritzing 0.9.3b)

parts:
  U1 = ESP8266 WiFi Module [part_number=ESP8266]
  Composant1 = FTDI Basic Programmer

nets:
  N1: U1.RXD, Composant1.TXO
  N2: U1.VCC, U1.RST, U1.CH_PD, Composant1.POWER
  N3: U1.GPIO_0, U1.GND
  N4: U1.TXD, Composant1.RXI

notes:
  esp01
  FTID(sélectionné bien le tension 3.3v)

custom parts:
  ESP8266 WiFi Module: Generic WiFi Module based on the ESP8266 with onboard PCB antenna and UART communications
